// Logisim project 4X4_MEMORY_READ_WRITE.circ as structural Verilog: 1 circuit, main circuit main
module main (
);

  wire clock_1_out, COLUMN_p3, COLUMN_p4, COLUMN_p5, COLUMN_p6, COLUMN_p7, dipswitch_1_p1, dipswitch_1_p2,
       dipswitch_1_p3, dipswitch_1_p4, n7404_1_pin10, n7404_2_pin10, n7404_3_pin10, n7404_4_pin10,
       n7404_6_pin4, n7404_6_pin6, n7404_6_pin8, n7404_7_pin10, n7404_8_pin10, n7404_9_pin10, n7404_10_pin10,
       n7404_11_pin10, n7404_12_pin10, n7404_13_pin10, n7404_14_pin10, n7404_15_pin10, n7404_16_pin10,
       n7404_17_pin10, n7404_18_pin10, n7408_1_pin7, n7408_1_pin11, n7408_1_pin12, n7408_1_pin13,
       n7408_1_pin14, n7408_2_pin3, n7408_2_pin6, n7408_2_pin8, n7408_2_pin11, n7408_3_pin11, n7408_3_pin13,
       n7408_4_pin11, n7408_4_pin13, n7408_5_pin11, n7408_5_pin13, n7408_6_pin1, n7408_6_pin4, n7408_6_pin10,
       n7408_6_pin13, n7408_7_pin1, n7408_7_pin4, n7408_7_pin10, n7408_7_pin13, n7408_8_pin1, n7408_8_pin4,
       n7408_8_pin10, n7408_8_pin13, n7408_9_pin1, n7408_9_pin4, n7408_9_pin10, n7408_9_pin13, n7408_10_pin3,
       n7408_10_pin6, n7408_10_pin8, n7408_10_pin11, n7408_11_pin3, n7408_11_pin6, n7408_11_pin8,
       n7408_11_pin11, n7408_12_pin3, n7408_12_pin6, n7408_12_pin8, n7408_12_pin11, n7408_13_pin3,
       n7408_13_pin6, n7408_13_pin8, n7408_13_pin11, n7408_14_pin3, n7408_14_pin5, n7408_14_pin11,
       n7408_15_pin3, n7408_15_pin11, n7408_16_pin11, n7408_16_pin13, n7408_17_pin11, n7408_17_pin13,
       n7408_18_pin11, n7408_18_pin13, n7408_19_pin11, n7408_19_pin13, n7408_20_pin1, n7408_20_pin4,
       n7408_20_pin10, n7408_20_pin13, n7408_21_pin1, n7408_21_pin4, n7408_21_pin10, n7408_21_pin13,
       n7408_22_pin1, n7408_22_pin4, n7408_22_pin10, n7408_22_pin13, n7408_23_pin1, n7408_23_pin4,
       n7408_23_pin10, n7408_23_pin13, n7408_24_pin3, n7408_24_pin11, n7408_25_pin3, n7408_25_pin11,
       n7408_26_pin3, n7408_26_pin6, n7408_26_pin8, n7408_26_pin11, n7408_27_pin3, n7408_27_pin6,
       n7408_27_pin8, n7408_27_pin11, n7408_28_pin3, n7408_28_pin6, n7408_28_pin8, n7408_28_pin11,
       n7408_29_pin3, n7408_29_pin6, n7408_29_pin8, n7408_29_pin11, n7408_30_pin3, n7408_30_pin6,
       n7408_30_pin8, n7408_30_pin11, n7408_31_pin3, n7408_31_pin6, n7408_31_pin8, n7408_31_pin11,
       n7408_32_pin3, n7408_32_pin6, n7408_32_pin8, n7408_32_pin11, n7408_33_pin3, n7408_33_pin6,
       n7408_33_pin8, n7408_33_pin11, n7408_34_pin11, n7408_35_pin11, n7408_36_pin11, n7408_37_pin11,
       n7408_38_pin1, n7408_38_pin4, n7408_38_pin10, n7408_38_pin13, n7408_39_pin1, n7408_39_pin4,
       n7408_39_pin10, n7408_39_pin13, n7408_40_pin1, n7408_40_pin4, n7408_40_pin10, n7408_40_pin13,
       n7408_41_pin1, n7408_41_pin4, n7408_41_pin10, n7408_41_pin13, n7408_42_pin3, n7408_42_pin6,
       n7408_42_pin8, n7408_42_pin11, n7408_43_pin3, n7408_43_pin6, n7408_43_pin8, n7408_43_pin11,
       n7408_44_pin3, n7408_44_pin6, n7408_44_pin8, n7408_44_pin11, n7408_45_pin3, n7408_45_pin6,
       n7408_45_pin8, n7408_45_pin11, n7408_46_pin11, n7408_47_pin11, n7408_48_pin11, n7408_49_pin11,
       n7408_50_pin1, n7408_50_pin4, n7408_50_pin10, n7408_50_pin13, n7408_51_pin1, n7408_51_pin4,
       n7408_51_pin10, n7408_51_pin13, n7408_52_pin1, n7408_52_pin4, n7408_52_pin10, n7408_52_pin13,
       n7408_53_pin1, n7408_53_pin4, n7408_53_pin10, n7408_53_pin13, n7408_54_pin3, n7408_54_pin6,
       n7408_54_pin8, n7408_54_pin11, n7408_55_pin3, n7408_55_pin6, n7408_55_pin8, n7408_55_pin11,
       n7408_56_pin3, n7408_56_pin6, n7408_56_pin8, n7408_56_pin11, n7408_57_pin3, n7408_57_pin6,
       n7408_57_pin8, n7408_57_pin11, n7432_1_pin1, n7432_1_pin3, n7432_1_pin4, n7432_1_pin6, n7432_1_pin8,
       n7432_1_pin10, n7432_1_pin11, n7432_1_pin13, n7432_2_pin1, n7432_2_pin3, n7432_2_pin4, n7432_2_pin6,
       n7432_2_pin8, n7432_2_pin10, n7432_2_pin11, n7432_2_pin13, n7432_3_pin1, n7432_3_pin3, n7432_3_pin4,
       n7432_3_pin6, n7432_3_pin8, n7432_3_pin10, n7432_3_pin11, n7432_3_pin13, n7432_4_pin1, n7432_4_pin3,
       n7432_4_pin4, n7432_4_pin6, n7432_4_pin8, n7432_4_pin10, n7432_4_pin11, n7432_4_pin13, n7432_5_pin1,
       n7432_5_pin3, n7432_5_pin4, n7432_5_pin6, n7432_5_pin8, n7432_5_pin10, n7432_5_pin11, n7432_5_pin13,
       n7432_6_pin1, n7432_6_pin3, n7432_6_pin4, n7432_6_pin6, n7432_6_pin8, n7432_6_pin10, n7432_6_pin11,
       n7432_6_pin13, n7432_7_pin1, n7432_7_pin3, n7432_7_pin4, n7432_7_pin6, n7432_7_pin8, n7432_7_pin10,
       n7432_7_pin11, n7432_7_pin13, n7432_8_pin1, n7432_8_pin3, n7432_8_pin4, n7432_8_pin6, n7432_8_pin8,
       n7432_8_pin10, n7432_8_pin11, n7432_8_pin13, n7432_9_pin1, n7432_9_pin3, n7432_9_pin4, n7432_9_pin6,
       n7432_9_pin8, n7432_9_pin10, n7432_9_pin11, n7432_9_pin13, n7432_10_pin1, n7432_10_pin3,
       n7432_10_pin4, n7432_10_pin6, n7432_10_pin8, n7432_10_pin10, n7432_10_pin11, n7432_10_pin13,
       n7432_11_pin1, n7432_11_pin3, n7432_11_pin4, n7432_11_pin6, n7432_11_pin8, n7432_11_pin10,
       n7432_11_pin11, n7432_11_pin13, n7432_12_pin1, n7432_12_pin3, n7432_12_pin4, n7432_12_pin6,
       n7432_12_pin8, n7432_12_pin10, n7432_12_pin11, n7432_12_pin13, n7432_13_pin1, n7432_13_pin3,
       n7432_13_pin4, n7432_13_pin6, n7432_13_pin8, n7432_13_pin10, n7432_13_pin11, n7432_13_pin13,
       n7432_14_pin1, n7432_14_pin3, n7432_14_pin4, n7432_14_pin6, n7432_14_pin8, n7432_14_pin10,
       n7432_14_pin11, n7432_14_pin13, n7432_15_pin1, n7432_15_pin3, n7432_15_pin4, n7432_15_pin6,
       n7432_15_pin8, n7432_15_pin10, n7432_15_pin11, n7432_15_pin13, n7432_16_pin1, n7432_16_pin3,
       n7432_16_pin4, n7432_16_pin6, n7432_16_pin8, n7432_16_pin10, n7432_16_pin11, n7432_16_pin13,
       n74139_1_pin4, n74139_1_pin5, n74139_1_pin6, n74139_1_pin7, n74139_1_pin9, n74139_1_pin10,
       n74139_1_pin11, n74139_1_pin12, n74139_1_pin13, n74139_1_pin14, ROW_p1, ROW_p2;

  Clock clock_1 (.out(clock_1_out));
  _7408 #(.ShowInternalStructure("true"), .VccGndPorts("true")) u_7408_1 (
    .pin7(n7408_1_pin7), .pin14(n7408_1_pin14), .pin13(n7408_1_pin13), .pin12(n7408_1_pin12),
    .pin11(n7408_1_pin11));  // open: pin1, pin2, pin3, pin4, pin5, pin6, pin10, pin9, pin8
  _7404 #(.ShowInternalStructure("true"), .VccGndPorts("true")) u_7404_1 (
    .pin7(n7408_1_pin7), .pin14(n7408_1_pin14), .pin11(n7408_1_pin11), .pin10(n7404_1_pin10));  // open: pin1, pin2, pin3, pin4, pin5, pin6, pin13, pin12, pin9, pin8
  // DipSwitch #(.number(4)) dipswitch_1: pin names not known; wires that end beside it: dipswitch_1_p1, dipswitch_1_p2, dipswitch_1_p3, dipswitch_1_p4
  // DipSwitch #(.number(1)) dipswitch_2: pin names not known; wires that end beside it: n7408_1_pin12
  _7408 #(.ShowInternalStructure("true"), .VccGndPorts("true")) u_7408_2 (
    .pin1(n7408_1_pin12), .pin2(dipswitch_1_p1), .pin3(n7408_2_pin3), .pin4(n7408_1_pin12),
    .pin5(dipswitch_1_p2), .pin6(n7408_2_pin6), .pin7(n7408_1_pin7), .pin14(n7408_1_pin14),
    .pin13(n7408_1_pin12), .pin12(dipswitch_1_p4), .pin11(n7408_2_pin11), .pin10(n7408_1_pin12),
    .pin9(dipswitch_1_p3), .pin8(n7408_2_pin8));
  _7408 #(.ShowInternalStructure("true"), .VccGndPorts("true")) u_7408_3 (
    .pin7(n7408_1_pin7), .pin14(n7408_1_pin14), .pin13(n7408_3_pin13), .pin12(n7408_1_pin12),
    .pin11(n7408_3_pin11));  // open: pin1, pin2, pin3, pin4, pin5, pin6, pin10, pin9, pin8
  _7404 #(.ShowInternalStructure("true"), .VccGndPorts("true")) u_7404_2 (
    .pin7(n7408_1_pin7), .pin14(n7408_1_pin14), .pin11(n7408_3_pin11), .pin10(n7404_2_pin10));  // open: pin1, pin2, pin3, pin4, pin5, pin6, pin13, pin12, pin9, pin8
  _7408 #(.ShowInternalStructure("true"), .VccGndPorts("true")) u_7408_4 (
    .pin7(n7408_1_pin7), .pin14(n7408_1_pin14), .pin13(n7408_4_pin13), .pin12(n7408_1_pin12),
    .pin11(n7408_4_pin11));  // open: pin1, pin2, pin3, pin4, pin5, pin6, pin10, pin9, pin8
  _7404 #(.ShowInternalStructure("true"), .VccGndPorts("true")) u_7404_3 (
    .pin7(n7408_1_pin7), .pin14(n7408_1_pin14), .pin11(n7408_4_pin11), .pin10(n7404_3_pin10));  // open: pin1, pin2, pin3, pin4, pin5, pin6, pin13, pin12, pin9, pin8
  _7408 #(.ShowInternalStructure("true"), .VccGndPorts("true")) u_7408_5 (
    .pin7(n7408_1_pin7), .pin14(n7408_1_pin14), .pin13(n7408_5_pin13), .pin12(n7408_1_pin12),
    .pin11(n7408_5_pin11));  // open: pin1, pin2, pin3, pin4, pin5, pin6, pin10, pin9, pin8
  _7404 #(.ShowInternalStructure("true"), .VccGndPorts("true")) u_7404_4 (
    .pin7(n7408_1_pin7), .pin14(n7408_1_pin14), .pin11(n7408_5_pin11), .pin10(n7404_4_pin10));  // open: pin1, pin2, pin3, pin4, pin5, pin6, pin13, pin12, pin9, pin8
  // DipSwitch #(.number(2)) ROW: pin names not known; wires that end beside it: ROW_p1, ROW_p2
  _7432 #(.ShowInternalStructure("true"), .VccGndPorts("true")) u_7432_1 (
    .pin1(n7432_1_pin1), .pin2(n7408_2_pin8), .pin3(n7432_1_pin3), .pin4(n7432_1_pin4), .pin5(n7408_2_pin11),
    .pin6(n7432_1_pin6), .pin7(n7408_1_pin7), .pin14(n7408_1_pin14), .pin13(n7432_1_pin13),
    .pin12(n7408_2_pin3), .pin11(n7432_1_pin11), .pin10(n7432_1_pin10), .pin9(n7408_2_pin6),
    .pin8(n7432_1_pin8));
  _7408 #(.ShowInternalStructure("true"), .VccGndPorts("true")) u_7408_6 (
    .pin1(n7408_6_pin1), .pin2(n7404_2_pin10), .pin3(n7432_1_pin13), .pin4(n7408_6_pin4),
    .pin5(n7404_2_pin10), .pin6(n7432_1_pin10), .pin7(n7408_1_pin7), .pin14(n7408_1_pin14),
    .pin13(n7408_6_pin13), .pin12(n7404_2_pin10), .pin11(n7432_1_pin4), .pin10(n7408_6_pin10),
    .pin9(n7404_2_pin10), .pin8(n7432_1_pin1));
  _7432 #(.ShowInternalStructure("true"), .VccGndPorts("true")) u_7432_2 (
    .pin1(n7432_2_pin1), .pin2(n7408_2_pin8), .pin3(n7432_2_pin3), .pin4(n7432_2_pin4), .pin5(n7408_2_pin11),
    .pin6(n7432_2_pin6), .pin7(n7408_1_pin7), .pin14(n7408_1_pin14), .pin13(n7432_2_pin13),
    .pin12(n7408_2_pin3), .pin11(n7432_2_pin11), .pin10(n7432_2_pin10), .pin9(n7408_2_pin6),
    .pin8(n7432_2_pin8));
  _7408 #(.ShowInternalStructure("true"), .VccGndPorts("true")) u_7408_7 (
    .pin1(n7408_7_pin1), .pin2(n7404_3_pin10), .pin3(n7432_2_pin13), .pin4(n7408_7_pin4),
    .pin5(n7404_3_pin10), .pin6(n7432_2_pin10), .pin7(n7408_1_pin7), .pin14(n7408_1_pin14),
    .pin13(n7408_7_pin13), .pin12(n7404_3_pin10), .pin11(n7432_2_pin4), .pin10(n7408_7_pin10),
    .pin9(n7404_3_pin10), .pin8(n7432_2_pin1));
  _7432 #(.ShowInternalStructure("true"), .VccGndPorts("true")) u_7432_3 (
    .pin1(n7432_3_pin1), .pin2(n7408_2_pin8), .pin3(n7432_3_pin3), .pin4(n7432_3_pin4), .pin5(n7408_2_pin11),
    .pin6(n7432_3_pin6), .pin7(n7408_1_pin7), .pin14(n7408_1_pin14), .pin13(n7432_3_pin13),
    .pin12(n7408_2_pin3), .pin11(n7432_3_pin11), .pin10(n7432_3_pin10), .pin9(n7408_2_pin6),
    .pin8(n7432_3_pin8));
  _7408 #(.ShowInternalStructure("true"), .VccGndPorts("true")) u_7408_8 (
    .pin1(n7408_8_pin1), .pin2(n7404_4_pin10), .pin3(n7432_3_pin13), .pin4(n7408_8_pin4),
    .pin5(n7404_4_pin10), .pin6(n7432_3_pin10), .pin7(n7408_1_pin7), .pin14(n7408_1_pin14),
    .pin13(n7408_8_pin13), .pin12(n7404_4_pin10), .pin11(n7432_3_pin4), .pin10(n7408_8_pin10),
    .pin9(n7404_4_pin10), .pin8(n7432_3_pin1));
  _7432 #(.ShowInternalStructure("true"), .VccGndPorts("true")) u_7432_4 (
    .pin1(n7432_4_pin1), .pin2(n7408_2_pin8), .pin3(n7432_4_pin3), .pin4(n7432_4_pin4), .pin5(n7408_2_pin11),
    .pin6(n7432_4_pin6), .pin7(n7408_1_pin7), .pin14(n7408_1_pin14), .pin13(n7432_4_pin13),
    .pin12(n7408_2_pin3), .pin11(n7432_4_pin11), .pin10(n7432_4_pin10), .pin9(n7408_2_pin6),
    .pin8(n7432_4_pin8));
  _7408 #(.ShowInternalStructure("true"), .VccGndPorts("true")) u_7408_9 (
    .pin1(n7408_9_pin1), .pin2(n7404_1_pin10), .pin3(n7432_4_pin13), .pin4(n7408_9_pin4),
    .pin5(n7404_1_pin10), .pin6(n7432_4_pin10), .pin7(n7408_1_pin7), .pin14(n7408_1_pin14),
    .pin13(n7408_9_pin13), .pin12(n7404_1_pin10), .pin11(n7432_4_pin4), .pin10(n7408_9_pin10),
    .pin9(n7404_1_pin10), .pin8(n7432_4_pin1));
  _74139 #(.ShowInternalStructure("true"), .VccGndPorts("true")) u_74139_1 (
    .pin1(n7408_1_pin7), .pin2(ROW_p1), .pin3(ROW_p2), .pin4(n74139_1_pin4), .pin5(n74139_1_pin5),
    .pin6(n74139_1_pin6), .pin7(n74139_1_pin7), .pin8(n7408_1_pin7), .pin16(n7408_1_pin14),
    .pin15(n7408_1_pin7), .pin14(n74139_1_pin14), .pin13(n74139_1_pin13), .pin12(n74139_1_pin12),
    .pin11(n74139_1_pin11), .pin10(n74139_1_pin10), .pin9(n74139_1_pin9));
  // DipSwitch #(.number(2)) COLUMN: pin names not known; wires that end beside it: n74139_1_pin14, n74139_1_pin13, COLUMN_p3, COLUMN_p4, COLUMN_p5, COLUMN_p6, COLUMN_p7
  _7404 #(.ShowInternalStructure("true"), .VccGndPorts("true")) u_7404_5 (
    .pin5(n74139_1_pin6), .pin6(COLUMN_p5), .pin7(n7408_1_pin7), .pin14(n7408_1_pin14),
    .pin13(n74139_1_pin7), .pin12(COLUMN_p6), .pin11(n74139_1_pin5), .pin10(COLUMN_p4), .pin9(n74139_1_pin4),
    .pin8(COLUMN_p3));  // open: pin1, pin2, pin3, pin4
  _74175 #(.ShowInternalStructure("true"), .VccGndPorts("true")) u_74175_1 (
    .pin2(n7408_6_pin1), .pin4(n7432_1_pin11), .pin5(n7432_1_pin8), .pin7(n7408_6_pin4), .pin8(n7408_1_pin7),
    .pin16(n7408_1_pin14), .pin15(n7408_6_pin13), .pin13(n7432_1_pin6), .pin12(n7432_1_pin3),
    .pin10(n7408_6_pin10), .pin9(clock_1_out));  // open: pin1, pin3, pin6, pin14, pin11
  _74175 #(.ShowInternalStructure("true"), .VccGndPorts("true")) u_74175_2 (
    .pin2(n7408_7_pin1), .pin4(n7432_2_pin11), .pin5(n7432_2_pin8), .pin7(n7408_7_pin4), .pin8(n7408_1_pin7),
    .pin16(n7408_1_pin14), .pin15(n7408_7_pin13), .pin13(n7432_2_pin6), .pin12(n7432_2_pin3),
    .pin10(n7408_7_pin10), .pin9(clock_1_out));  // open: pin1, pin3, pin6, pin14, pin11
  _74175 #(.ShowInternalStructure("true"), .VccGndPorts("true")) u_74175_3 (
    .pin2(n7408_8_pin1), .pin4(n7432_3_pin11), .pin5(n7432_3_pin8), .pin7(n7408_8_pin4), .pin8(n7408_1_pin7),
    .pin16(n7408_1_pin14), .pin15(n7408_8_pin13), .pin13(n7432_3_pin6), .pin12(n7432_3_pin3),
    .pin10(n7408_8_pin10), .pin9(clock_1_out));  // open: pin1, pin3, pin6, pin14, pin11
  _74175 #(.ShowInternalStructure("true"), .VccGndPorts("true")) u_74175_4 (
    .pin2(n7408_9_pin1), .pin4(n7432_4_pin11), .pin5(n7432_4_pin8), .pin7(n7408_9_pin4), .pin8(n7408_1_pin7),
    .pin16(n7408_1_pin14), .pin15(n7408_9_pin13), .pin13(n7432_4_pin6), .pin12(n7432_4_pin3),
    .pin10(n7408_9_pin10), .pin9(clock_1_out));  // open: pin1, pin3, pin6, pin14, pin11
  _7404 #(.ShowInternalStructure("true"), .VccGndPorts("true")) u_7404_6 (
    .pin1(n74139_1_pin12), .pin2(COLUMN_p7), .pin3(n74139_1_pin11), .pin4(n7404_6_pin4),
    .pin5(n74139_1_pin10), .pin6(n7404_6_pin6), .pin7(n7408_1_pin7), .pin14(n7408_1_pin14),
    .pin9(n74139_1_pin9), .pin8(n7404_6_pin8));  // open: pin13, pin12, pin11, pin10
  LedBar #(.matrixcols(4)) ledbar_1 (
    .led0(n7408_10_pin3), .led1(n7408_10_pin6), .led2(n7408_10_pin8), .led3(n7408_10_pin11));
  LedBar #(.matrixcols(4)) ledbar_2 (
    .led0(n7408_11_pin3), .led1(n7408_11_pin6), .led2(n7408_11_pin8), .led3(n7408_11_pin11));
  LedBar #(.matrixcols(4)) ledbar_3 (
    .led0(n7408_12_pin3), .led1(n7408_12_pin6), .led2(n7408_12_pin8), .led3(n7408_12_pin11));
  LedBar #(.matrixcols(4)) ledbar_4 (
    .led0(n7408_13_pin3), .led1(n7408_13_pin6), .led2(n7408_13_pin8), .led3(n7408_13_pin11));
  _7408 #(.ShowInternalStructure("true"), .VccGndPorts("true")) u_7408_10 (
    .pin1(n7408_4_pin13), .pin2(n7408_7_pin1), .pin3(n7408_10_pin3), .pin4(n7408_4_pin13),
    .pin5(n7408_7_pin4), .pin6(n7408_10_pin6), .pin7(n7408_1_pin7), .pin14(n7408_1_pin14),
    .pin13(n7408_4_pin13), .pin12(n7408_7_pin13), .pin11(n7408_10_pin11), .pin10(n7408_4_pin13),
    .pin9(n7408_7_pin10), .pin8(n7408_10_pin8));
  _7408 #(.ShowInternalStructure("true"), .VccGndPorts("true")) u_7408_11 (
    .pin1(n7408_5_pin13), .pin2(n7408_8_pin1), .pin3(n7408_11_pin3), .pin4(n7408_5_pin13),
    .pin5(n7408_8_pin4), .pin6(n7408_11_pin6), .pin7(n7408_1_pin7), .pin14(n7408_1_pin14),
    .pin13(n7408_5_pin13), .pin12(n7408_8_pin13), .pin11(n7408_11_pin11), .pin10(n7408_5_pin13),
    .pin9(n7408_8_pin10), .pin8(n7408_11_pin8));
  _7408 #(.ShowInternalStructure("true"), .VccGndPorts("true")) u_7408_12 (
    .pin1(n7408_1_pin13), .pin2(n7408_9_pin1), .pin3(n7408_12_pin3), .pin4(n7408_1_pin13),
    .pin5(n7408_9_pin4), .pin6(n7408_12_pin6), .pin7(n7408_1_pin7), .pin14(n7408_1_pin14),
    .pin13(n7408_1_pin13), .pin12(n7408_9_pin13), .pin11(n7408_12_pin11), .pin10(n7408_1_pin13),
    .pin9(n7408_9_pin10), .pin8(n7408_12_pin8));
  _7408 #(.ShowInternalStructure("true"), .VccGndPorts("true")) u_7408_13 (
    .pin1(n7408_3_pin13), .pin2(n7408_6_pin1), .pin3(n7408_13_pin3), .pin4(n7408_3_pin13),
    .pin5(n7408_6_pin4), .pin6(n7408_13_pin6), .pin7(n7408_1_pin7), .pin14(n7408_1_pin14),
    .pin13(n7408_3_pin13), .pin12(n7408_6_pin13), .pin11(n7408_13_pin11), .pin10(n7408_3_pin13),
    .pin9(n7408_6_pin10), .pin8(n7408_13_pin8));
  _7408 #(.ShowInternalStructure("true"), .VccGndPorts("true")) u_7408_14 (
    .pin1(COLUMN_p7), .pin2(COLUMN_p3), .pin3(n7408_14_pin3), .pin4(n7408_14_pin3), .pin5(n7408_14_pin5),
    .pin6(n7408_3_pin13), .pin7(n7408_1_pin7), .pin14(n7408_1_pin14), .pin13(COLUMN_p7), .pin12(COLUMN_p4),
    .pin11(n7408_14_pin11), .pin10(n7408_14_pin11), .pin9(n7408_14_pin5), .pin8(n7408_4_pin13));
  _7408 #(.ShowInternalStructure("true"), .VccGndPorts("true")) u_7408_15 (
    .pin1(COLUMN_p7), .pin2(COLUMN_p5), .pin3(n7408_15_pin3), .pin4(n7408_15_pin3), .pin5(n7408_14_pin5),
    .pin6(n7408_5_pin13), .pin7(n7408_1_pin7), .pin14(n7408_1_pin14), .pin13(COLUMN_p7), .pin12(COLUMN_p6),
    .pin11(n7408_15_pin11), .pin10(n7408_15_pin11), .pin9(n7408_14_pin5), .pin8(n7408_1_pin13));
  _7408 #(.ShowInternalStructure("true"), .VccGndPorts("true")) u_7408_16 (
    .pin7(n7408_1_pin7), .pin14(n7408_1_pin14), .pin13(n7408_16_pin13), .pin12(n7408_1_pin12),
    .pin11(n7408_16_pin11));  // open: pin1, pin2, pin3, pin4, pin5, pin6, pin10, pin9, pin8
  _7404 #(.ShowInternalStructure("true"), .VccGndPorts("true")) u_7404_7 (
    .pin7(n7408_1_pin7), .pin14(n7408_1_pin14), .pin11(n7408_16_pin11), .pin10(n7404_7_pin10));  // open: pin1, pin2, pin3, pin4, pin5, pin6, pin13, pin12, pin9, pin8
  _7408 #(.ShowInternalStructure("true"), .VccGndPorts("true")) u_7408_17 (
    .pin7(n7408_1_pin7), .pin14(n7408_1_pin14), .pin13(n7408_17_pin13), .pin12(n7408_1_pin12),
    .pin11(n7408_17_pin11));  // open: pin1, pin2, pin3, pin4, pin5, pin6, pin10, pin9, pin8
  _7404 #(.ShowInternalStructure("true"), .VccGndPorts("true")) u_7404_8 (
    .pin7(n7408_1_pin7), .pin14(n7408_1_pin14), .pin11(n7408_17_pin11), .pin10(n7404_8_pin10));  // open: pin1, pin2, pin3, pin4, pin5, pin6, pin13, pin12, pin9, pin8
  _7408 #(.ShowInternalStructure("true"), .VccGndPorts("true")) u_7408_18 (
    .pin7(n7408_1_pin7), .pin14(n7408_1_pin14), .pin13(n7408_18_pin13), .pin12(n7408_1_pin12),
    .pin11(n7408_18_pin11));  // open: pin1, pin2, pin3, pin4, pin5, pin6, pin10, pin9, pin8
  _7404 #(.ShowInternalStructure("true"), .VccGndPorts("true")) u_7404_9 (
    .pin7(n7408_1_pin7), .pin14(n7408_1_pin14), .pin11(n7408_18_pin11), .pin10(n7404_9_pin10));  // open: pin1, pin2, pin3, pin4, pin5, pin6, pin13, pin12, pin9, pin8
  _7408 #(.ShowInternalStructure("true"), .VccGndPorts("true")) u_7408_19 (
    .pin7(n7408_1_pin7), .pin14(n7408_1_pin14), .pin13(n7408_19_pin13), .pin12(n7408_1_pin12),
    .pin11(n7408_19_pin11));  // open: pin1, pin2, pin3, pin4, pin5, pin6, pin10, pin9, pin8
  _7404 #(.ShowInternalStructure("true"), .VccGndPorts("true")) u_7404_10 (
    .pin7(n7408_1_pin7), .pin14(n7408_1_pin14), .pin11(n7408_19_pin11), .pin10(n7404_10_pin10));  // open: pin1, pin2, pin3, pin4, pin5, pin6, pin13, pin12, pin9, pin8
  _7432 #(.ShowInternalStructure("true"), .VccGndPorts("true")) u_7432_5 (
    .pin1(n7432_5_pin1), .pin2(n7408_2_pin8), .pin3(n7432_5_pin3), .pin4(n7432_5_pin4), .pin5(n7408_2_pin11),
    .pin6(n7432_5_pin6), .pin7(n7408_1_pin7), .pin14(n7408_1_pin14), .pin13(n7432_5_pin13),
    .pin12(n7408_2_pin3), .pin11(n7432_5_pin11), .pin10(n7432_5_pin10), .pin9(n7408_2_pin6),
    .pin8(n7432_5_pin8));
  _7408 #(.ShowInternalStructure("true"), .VccGndPorts("true")) u_7408_20 (
    .pin1(n7408_20_pin1), .pin2(n7404_8_pin10), .pin3(n7432_5_pin13), .pin4(n7408_20_pin4),
    .pin5(n7404_8_pin10), .pin6(n7432_5_pin10), .pin7(n7408_1_pin7), .pin14(n7408_1_pin14),
    .pin13(n7408_20_pin13), .pin12(n7404_8_pin10), .pin11(n7432_5_pin4), .pin10(n7408_20_pin10),
    .pin9(n7404_8_pin10), .pin8(n7432_5_pin1));
  _7432 #(.ShowInternalStructure("true"), .VccGndPorts("true")) u_7432_6 (
    .pin1(n7432_6_pin1), .pin2(n7408_2_pin8), .pin3(n7432_6_pin3), .pin4(n7432_6_pin4), .pin5(n7408_2_pin11),
    .pin6(n7432_6_pin6), .pin7(n7408_1_pin7), .pin14(n7408_1_pin14), .pin13(n7432_6_pin13),
    .pin12(n7408_2_pin3), .pin11(n7432_6_pin11), .pin10(n7432_6_pin10), .pin9(n7408_2_pin6),
    .pin8(n7432_6_pin8));
  _7408 #(.ShowInternalStructure("true"), .VccGndPorts("true")) u_7408_21 (
    .pin1(n7408_21_pin1), .pin2(n7404_9_pin10), .pin3(n7432_6_pin13), .pin4(n7408_21_pin4),
    .pin5(n7404_9_pin10), .pin6(n7432_6_pin10), .pin7(n7408_1_pin7), .pin14(n7408_1_pin14),
    .pin13(n7408_21_pin13), .pin12(n7404_9_pin10), .pin11(n7432_6_pin4), .pin10(n7408_21_pin10),
    .pin9(n7404_9_pin10), .pin8(n7432_6_pin1));
  _7432 #(.ShowInternalStructure("true"), .VccGndPorts("true")) u_7432_7 (
    .pin1(n7432_7_pin1), .pin2(n7408_2_pin8), .pin3(n7432_7_pin3), .pin4(n7432_7_pin4), .pin5(n7408_2_pin11),
    .pin6(n7432_7_pin6), .pin7(n7408_1_pin7), .pin14(n7408_1_pin14), .pin13(n7432_7_pin13),
    .pin12(n7408_2_pin3), .pin11(n7432_7_pin11), .pin10(n7432_7_pin10), .pin9(n7408_2_pin6),
    .pin8(n7432_7_pin8));
  _7408 #(.ShowInternalStructure("true"), .VccGndPorts("true")) u_7408_22 (
    .pin1(n7408_22_pin1), .pin2(n7404_10_pin10), .pin3(n7432_7_pin13), .pin4(n7408_22_pin4),
    .pin5(n7404_10_pin10), .pin6(n7432_7_pin10), .pin7(n7408_1_pin7), .pin14(n7408_1_pin14),
    .pin13(n7408_22_pin13), .pin12(n7404_10_pin10), .pin11(n7432_7_pin4), .pin10(n7408_22_pin10),
    .pin9(n7404_10_pin10), .pin8(n7432_7_pin1));
  _7432 #(.ShowInternalStructure("true"), .VccGndPorts("true")) u_7432_8 (
    .pin1(n7432_8_pin1), .pin2(n7408_2_pin8), .pin3(n7432_8_pin3), .pin4(n7432_8_pin4), .pin5(n7408_2_pin11),
    .pin6(n7432_8_pin6), .pin7(n7408_1_pin7), .pin14(n7408_1_pin14), .pin13(n7432_8_pin13),
    .pin12(n7408_2_pin3), .pin11(n7432_8_pin11), .pin10(n7432_8_pin10), .pin9(n7408_2_pin6),
    .pin8(n7432_8_pin8));
  _7408 #(.ShowInternalStructure("true"), .VccGndPorts("true")) u_7408_23 (
    .pin1(n7408_23_pin1), .pin2(n7404_7_pin10), .pin3(n7432_8_pin13), .pin4(n7408_23_pin4),
    .pin5(n7404_7_pin10), .pin6(n7432_8_pin10), .pin7(n7408_1_pin7), .pin14(n7408_1_pin14),
    .pin13(n7408_23_pin13), .pin12(n7404_7_pin10), .pin11(n7432_8_pin4), .pin10(n7408_23_pin10),
    .pin9(n7404_7_pin10), .pin8(n7432_8_pin1));
  _7408 #(.ShowInternalStructure("true"), .VccGndPorts("true")) u_7408_24 (
    .pin1(n7404_6_pin4), .pin2(COLUMN_p3), .pin3(n7408_24_pin3), .pin4(n7408_24_pin3), .pin5(n7408_14_pin5),
    .pin6(n7408_17_pin13), .pin7(n7408_1_pin7), .pin14(n7408_1_pin14), .pin13(n7404_6_pin4),
    .pin12(COLUMN_p4), .pin11(n7408_24_pin11), .pin10(n7408_24_pin11), .pin9(n7408_14_pin5),
    .pin8(n7408_18_pin13));
  _7408 #(.ShowInternalStructure("true"), .VccGndPorts("true")) u_7408_25 (
    .pin1(n7404_6_pin4), .pin2(COLUMN_p5), .pin3(n7408_25_pin3), .pin4(n7408_25_pin3), .pin5(n7408_14_pin5),
    .pin6(n7408_19_pin13), .pin7(n7408_1_pin7), .pin14(n7408_1_pin14), .pin13(n7404_6_pin4),
    .pin12(COLUMN_p6), .pin11(n7408_25_pin11), .pin10(n7408_25_pin11), .pin9(n7408_14_pin5),
    .pin8(n7408_16_pin13));
  _74175 #(.ShowInternalStructure("true"), .VccGndPorts("true")) u_74175_5 (
    .pin2(n7408_20_pin1), .pin4(n7432_5_pin11), .pin5(n7432_5_pin8), .pin7(n7408_20_pin4),
    .pin8(n7408_1_pin7), .pin16(n7408_1_pin14), .pin15(n7408_20_pin13), .pin13(n7432_5_pin6),
    .pin12(n7432_5_pin3), .pin10(n7408_20_pin10), .pin9(clock_1_out));  // open: pin1, pin3, pin6, pin14, pin11
  _74175 #(.ShowInternalStructure("true"), .VccGndPorts("true")) u_74175_6 (
    .pin2(n7408_21_pin1), .pin4(n7432_6_pin11), .pin5(n7432_6_pin8), .pin7(n7408_21_pin4),
    .pin8(n7408_1_pin7), .pin16(n7408_1_pin14), .pin15(n7408_21_pin13), .pin13(n7432_6_pin6),
    .pin12(n7432_6_pin3), .pin10(n7408_21_pin10), .pin9(clock_1_out));  // open: pin1, pin3, pin6, pin14, pin11
  _74175 #(.ShowInternalStructure("true"), .VccGndPorts("true")) u_74175_7 (
    .pin2(n7408_22_pin1), .pin4(n7432_7_pin11), .pin5(n7432_7_pin8), .pin7(n7408_22_pin4),
    .pin8(n7408_1_pin7), .pin16(n7408_1_pin14), .pin15(n7408_22_pin13), .pin13(n7432_7_pin6),
    .pin12(n7432_7_pin3), .pin10(n7408_22_pin10), .pin9(clock_1_out));  // open: pin1, pin3, pin6, pin14, pin11
  _74175 #(.ShowInternalStructure("true"), .VccGndPorts("true")) u_74175_8 (
    .pin2(n7408_23_pin1), .pin4(n7432_8_pin11), .pin5(n7432_8_pin8), .pin7(n7408_23_pin4),
    .pin8(n7408_1_pin7), .pin16(n7408_1_pin14), .pin15(n7408_23_pin13), .pin13(n7432_8_pin6),
    .pin12(n7432_8_pin3), .pin10(n7408_23_pin10), .pin9(clock_1_out));  // open: pin1, pin3, pin6, pin14, pin11
  LedBar #(.matrixcols(4)) ledbar_5 (
    .led0(n7408_28_pin3), .led1(n7408_28_pin6), .led2(n7408_28_pin8), .led3(n7408_28_pin11));
  LedBar #(.matrixcols(4)) ledbar_6 (
    .led0(n7408_29_pin3), .led1(n7408_29_pin6), .led2(n7408_29_pin8), .led3(n7408_29_pin11));
  LedBar #(.matrixcols(4)) ledbar_7 (
    .led0(n7408_30_pin3), .led1(n7408_30_pin6), .led2(n7408_30_pin8), .led3(n7408_30_pin11));
  _7408 #(.ShowInternalStructure("true"), .VccGndPorts("true")) u_7408_26 (
    .pin1(n7404_6_pin6), .pin2(COLUMN_p3), .pin3(n7408_26_pin3), .pin4(n7408_26_pin3), .pin5(n7408_14_pin5),
    .pin6(n7408_26_pin6), .pin7(n7408_1_pin7), .pin14(n7408_1_pin14), .pin13(n7404_6_pin6),
    .pin12(COLUMN_p4), .pin11(n7408_26_pin11), .pin10(n7408_26_pin11), .pin9(n7408_14_pin5),
    .pin8(n7408_26_pin8));
  _7408 #(.ShowInternalStructure("true"), .VccGndPorts("true")) u_7408_27 (
    .pin1(n7404_6_pin6), .pin2(COLUMN_p5), .pin3(n7408_27_pin3), .pin4(n7408_27_pin3), .pin5(n7408_14_pin5),
    .pin6(n7408_27_pin6), .pin7(n7408_1_pin7), .pin14(n7408_1_pin14), .pin13(n7404_6_pin6),
    .pin12(COLUMN_p6), .pin11(n7408_27_pin11), .pin10(n7408_27_pin11), .pin9(n7408_14_pin5),
    .pin8(n7408_27_pin8));
  LedBar #(.matrixcols(4)) ledbar_8 (
    .led0(n7408_31_pin3), .led1(n7408_31_pin6), .led2(n7408_31_pin8), .led3(n7408_31_pin11));
  _7408 #(.ShowInternalStructure("true"), .VccGndPorts("true")) u_7408_28 (
    .pin1(n7408_18_pin13), .pin2(n7408_21_pin1), .pin3(n7408_28_pin3), .pin4(n7408_18_pin13),
    .pin5(n7408_21_pin4), .pin6(n7408_28_pin6), .pin7(n7408_1_pin7), .pin14(n7408_1_pin14),
    .pin13(n7408_18_pin13), .pin12(n7408_21_pin13), .pin11(n7408_28_pin11), .pin10(n7408_18_pin13),
    .pin9(n7408_21_pin10), .pin8(n7408_28_pin8));
  _7408 #(.ShowInternalStructure("true"), .VccGndPorts("true")) u_7408_29 (
    .pin1(n7408_19_pin13), .pin2(n7408_22_pin1), .pin3(n7408_29_pin3), .pin4(n7408_19_pin13),
    .pin5(n7408_22_pin4), .pin6(n7408_29_pin6), .pin7(n7408_1_pin7), .pin14(n7408_1_pin14),
    .pin13(n7408_19_pin13), .pin12(n7408_22_pin13), .pin11(n7408_29_pin11), .pin10(n7408_19_pin13),
    .pin9(n7408_22_pin10), .pin8(n7408_29_pin8));
  _7408 #(.ShowInternalStructure("true"), .VccGndPorts("true")) u_7408_30 (
    .pin1(n7408_16_pin13), .pin2(n7408_23_pin1), .pin3(n7408_30_pin3), .pin4(n7408_16_pin13),
    .pin5(n7408_23_pin4), .pin6(n7408_30_pin6), .pin7(n7408_1_pin7), .pin14(n7408_1_pin14),
    .pin13(n7408_16_pin13), .pin12(n7408_23_pin13), .pin11(n7408_30_pin11), .pin10(n7408_16_pin13),
    .pin9(n7408_23_pin10), .pin8(n7408_30_pin8));
  _7408 #(.ShowInternalStructure("true"), .VccGndPorts("true")) u_7408_31 (
    .pin1(n7408_17_pin13), .pin2(n7408_20_pin1), .pin3(n7408_31_pin3), .pin4(n7408_17_pin13),
    .pin5(n7408_20_pin4), .pin6(n7408_31_pin6), .pin7(n7408_1_pin7), .pin14(n7408_1_pin14),
    .pin13(n7408_17_pin13), .pin12(n7408_20_pin13), .pin11(n7408_31_pin11), .pin10(n7408_17_pin13),
    .pin9(n7408_20_pin10), .pin8(n7408_31_pin8));
  _7408 #(.ShowInternalStructure("true"), .VccGndPorts("true")) u_7408_32 (
    .pin1(n7404_6_pin8), .pin2(COLUMN_p3), .pin3(n7408_32_pin3), .pin4(n7408_32_pin3), .pin5(n7408_14_pin5),
    .pin6(n7408_32_pin6), .pin7(n7408_1_pin7), .pin14(n7408_1_pin14), .pin13(n7404_6_pin8),
    .pin12(COLUMN_p4), .pin11(n7408_32_pin11), .pin10(n7408_32_pin11), .pin9(n7408_14_pin5),
    .pin8(n7408_32_pin8));
  _7408 #(.ShowInternalStructure("true"), .VccGndPorts("true")) u_7408_33 (
    .pin1(n7404_6_pin8), .pin2(COLUMN_p5), .pin3(n7408_33_pin3), .pin4(n7408_33_pin3), .pin5(n7408_14_pin5),
    .pin6(n7408_33_pin6), .pin7(n7408_1_pin7), .pin14(n7408_1_pin14), .pin13(n7404_6_pin8),
    .pin12(COLUMN_p6), .pin11(n7408_33_pin11), .pin10(n7408_33_pin11), .pin9(n7408_14_pin5),
    .pin8(n7408_33_pin8));
  _7408 #(.ShowInternalStructure("true"), .VccGndPorts("true")) u_7408_34 (
    .pin7(n7408_1_pin7), .pin14(n7408_1_pin14), .pin13(n7408_26_pin6), .pin12(n7408_1_pin12),
    .pin11(n7408_34_pin11));  // open: pin1, pin2, pin3, pin4, pin5, pin6, pin10, pin9, pin8
  _7404 #(.ShowInternalStructure("true"), .VccGndPorts("true")) u_7404_11 (
    .pin7(n7408_1_pin7), .pin14(n7408_1_pin14), .pin11(n7408_34_pin11), .pin10(n7404_11_pin10));  // open: pin1, pin2, pin3, pin4, pin5, pin6, pin13, pin12, pin9, pin8
  _7408 #(.ShowInternalStructure("true"), .VccGndPorts("true")) u_7408_35 (
    .pin7(n7408_1_pin7), .pin14(n7408_1_pin14), .pin13(n7408_26_pin8), .pin12(n7408_1_pin12),
    .pin11(n7408_35_pin11));  // open: pin1, pin2, pin3, pin4, pin5, pin6, pin10, pin9, pin8
  _7404 #(.ShowInternalStructure("true"), .VccGndPorts("true")) u_7404_12 (
    .pin7(n7408_1_pin7), .pin14(n7408_1_pin14), .pin11(n7408_35_pin11), .pin10(n7404_12_pin10));  // open: pin1, pin2, pin3, pin4, pin5, pin6, pin13, pin12, pin9, pin8
  _7408 #(.ShowInternalStructure("true"), .VccGndPorts("true")) u_7408_36 (
    .pin7(n7408_1_pin7), .pin14(n7408_1_pin14), .pin13(n7408_27_pin6), .pin12(n7408_1_pin12),
    .pin11(n7408_36_pin11));  // open: pin1, pin2, pin3, pin4, pin5, pin6, pin10, pin9, pin8
  _7404 #(.ShowInternalStructure("true"), .VccGndPorts("true")) u_7404_13 (
    .pin7(n7408_1_pin7), .pin14(n7408_1_pin14), .pin11(n7408_36_pin11), .pin10(n7404_13_pin10));  // open: pin1, pin2, pin3, pin4, pin5, pin6, pin13, pin12, pin9, pin8
  _7408 #(.ShowInternalStructure("true"), .VccGndPorts("true")) u_7408_37 (
    .pin7(n7408_1_pin7), .pin14(n7408_1_pin14), .pin13(n7408_27_pin8), .pin12(n7408_1_pin12),
    .pin11(n7408_37_pin11));  // open: pin1, pin2, pin3, pin4, pin5, pin6, pin10, pin9, pin8
  _7404 #(.ShowInternalStructure("true"), .VccGndPorts("true")) u_7404_14 (
    .pin7(n7408_1_pin7), .pin14(n7408_1_pin14), .pin11(n7408_37_pin11), .pin10(n7404_14_pin10));  // open: pin1, pin2, pin3, pin4, pin5, pin6, pin13, pin12, pin9, pin8
  _7432 #(.ShowInternalStructure("true"), .VccGndPorts("true")) u_7432_9 (
    .pin1(n7432_9_pin1), .pin2(n7408_2_pin8), .pin3(n7432_9_pin3), .pin4(n7432_9_pin4), .pin5(n7408_2_pin11),
    .pin6(n7432_9_pin6), .pin7(n7408_1_pin7), .pin14(n7408_1_pin14), .pin13(n7432_9_pin13),
    .pin12(n7408_2_pin3), .pin11(n7432_9_pin11), .pin10(n7432_9_pin10), .pin9(n7408_2_pin6),
    .pin8(n7432_9_pin8));
  _7408 #(.ShowInternalStructure("true"), .VccGndPorts("true")) u_7408_38 (
    .pin1(n7408_38_pin1), .pin2(n7404_11_pin10), .pin3(n7432_9_pin13), .pin4(n7408_38_pin4),
    .pin5(n7404_11_pin10), .pin6(n7432_9_pin10), .pin7(n7408_1_pin7), .pin14(n7408_1_pin14),
    .pin13(n7408_38_pin13), .pin12(n7404_11_pin10), .pin11(n7432_9_pin4), .pin10(n7408_38_pin10),
    .pin9(n7404_11_pin10), .pin8(n7432_9_pin1));
  _7432 #(.ShowInternalStructure("true"), .VccGndPorts("true")) u_7432_10 (
    .pin1(n7432_10_pin1), .pin2(n7408_2_pin8), .pin3(n7432_10_pin3), .pin4(n7432_10_pin4),
    .pin5(n7408_2_pin11), .pin6(n7432_10_pin6), .pin7(n7408_1_pin7), .pin14(n7408_1_pin14),
    .pin13(n7432_10_pin13), .pin12(n7408_2_pin3), .pin11(n7432_10_pin11), .pin10(n7432_10_pin10),
    .pin9(n7408_2_pin6), .pin8(n7432_10_pin8));
  _7408 #(.ShowInternalStructure("true"), .VccGndPorts("true")) u_7408_39 (
    .pin1(n7408_39_pin1), .pin2(n7404_12_pin10), .pin3(n7432_10_pin13), .pin4(n7408_39_pin4),
    .pin5(n7404_12_pin10), .pin6(n7432_10_pin10), .pin7(n7408_1_pin7), .pin14(n7408_1_pin14),
    .pin13(n7408_39_pin13), .pin12(n7404_12_pin10), .pin11(n7432_10_pin4), .pin10(n7408_39_pin10),
    .pin9(n7404_12_pin10), .pin8(n7432_10_pin1));
  _7432 #(.ShowInternalStructure("true"), .VccGndPorts("true")) u_7432_11 (
    .pin1(n7432_11_pin1), .pin2(n7408_2_pin8), .pin3(n7432_11_pin3), .pin4(n7432_11_pin4),
    .pin5(n7408_2_pin11), .pin6(n7432_11_pin6), .pin7(n7408_1_pin7), .pin14(n7408_1_pin14),
    .pin13(n7432_11_pin13), .pin12(n7408_2_pin3), .pin11(n7432_11_pin11), .pin10(n7432_11_pin10),
    .pin9(n7408_2_pin6), .pin8(n7432_11_pin8));
  _7408 #(.ShowInternalStructure("true"), .VccGndPorts("true")) u_7408_40 (
    .pin1(n7408_40_pin1), .pin2(n7404_13_pin10), .pin3(n7432_11_pin13), .pin4(n7408_40_pin4),
    .pin5(n7404_13_pin10), .pin6(n7432_11_pin10), .pin7(n7408_1_pin7), .pin14(n7408_1_pin14),
    .pin13(n7408_40_pin13), .pin12(n7404_13_pin10), .pin11(n7432_11_pin4), .pin10(n7408_40_pin10),
    .pin9(n7404_13_pin10), .pin8(n7432_11_pin1));
  _7432 #(.ShowInternalStructure("true"), .VccGndPorts("true")) u_7432_12 (
    .pin1(n7432_12_pin1), .pin2(n7408_2_pin8), .pin3(n7432_12_pin3), .pin4(n7432_12_pin4),
    .pin5(n7408_2_pin11), .pin6(n7432_12_pin6), .pin7(n7408_1_pin7), .pin14(n7408_1_pin14),
    .pin13(n7432_12_pin13), .pin12(n7408_2_pin3), .pin11(n7432_12_pin11), .pin10(n7432_12_pin10),
    .pin9(n7408_2_pin6), .pin8(n7432_12_pin8));
  _7408 #(.ShowInternalStructure("true"), .VccGndPorts("true")) u_7408_41 (
    .pin1(n7408_41_pin1), .pin2(n7404_14_pin10), .pin3(n7432_12_pin13), .pin4(n7408_41_pin4),
    .pin5(n7404_14_pin10), .pin6(n7432_12_pin10), .pin7(n7408_1_pin7), .pin14(n7408_1_pin14),
    .pin13(n7408_41_pin13), .pin12(n7404_14_pin10), .pin11(n7432_12_pin4), .pin10(n7408_41_pin10),
    .pin9(n7404_14_pin10), .pin8(n7432_12_pin1));
  _74175 #(.ShowInternalStructure("true"), .VccGndPorts("true")) u_74175_9 (
    .pin2(n7408_38_pin1), .pin4(n7432_9_pin11), .pin5(n7432_9_pin8), .pin7(n7408_38_pin4),
    .pin8(n7408_1_pin7), .pin16(n7408_1_pin14), .pin15(n7408_38_pin13), .pin13(n7432_9_pin6),
    .pin12(n7432_9_pin3), .pin10(n7408_38_pin10), .pin9(clock_1_out));  // open: pin1, pin3, pin6, pin14, pin11
  _74175 #(.ShowInternalStructure("true"), .VccGndPorts("true")) u_74175_10 (
    .pin2(n7408_39_pin1), .pin4(n7432_10_pin11), .pin5(n7432_10_pin8), .pin7(n7408_39_pin4),
    .pin8(n7408_1_pin7), .pin16(n7408_1_pin14), .pin15(n7408_39_pin13), .pin13(n7432_10_pin6),
    .pin12(n7432_10_pin3), .pin10(n7408_39_pin10), .pin9(clock_1_out));  // open: pin1, pin3, pin6, pin14, pin11
  _74175 #(.ShowInternalStructure("true"), .VccGndPorts("true")) u_74175_11 (
    .pin2(n7408_40_pin1), .pin4(n7432_11_pin11), .pin5(n7432_11_pin8), .pin7(n7408_40_pin4),
    .pin8(n7408_1_pin7), .pin16(n7408_1_pin14), .pin15(n7408_40_pin13), .pin13(n7432_11_pin6),
    .pin12(n7432_11_pin3), .pin10(n7408_40_pin10), .pin9(clock_1_out));  // open: pin1, pin3, pin6, pin14, pin11
  _74175 #(.ShowInternalStructure("true"), .VccGndPorts("true")) u_74175_12 (
    .pin2(n7408_41_pin1), .pin4(n7432_12_pin11), .pin5(n7432_12_pin8), .pin7(n7408_41_pin4),
    .pin8(n7408_1_pin7), .pin16(n7408_1_pin14), .pin15(n7408_41_pin13), .pin13(n7432_12_pin6),
    .pin12(n7432_12_pin3), .pin10(n7408_41_pin10), .pin9(clock_1_out));  // open: pin1, pin3, pin6, pin14, pin11
  LedBar #(.matrixcols(4)) ledbar_9 (
    .led0(n7408_42_pin3), .led1(n7408_42_pin6), .led2(n7408_42_pin8), .led3(n7408_42_pin11));
  LedBar #(.matrixcols(4)) ledbar_10 (
    .led0(n7408_43_pin3), .led1(n7408_43_pin6), .led2(n7408_43_pin8), .led3(n7408_43_pin11));
  LedBar #(.matrixcols(4)) ledbar_11 (
    .led0(n7408_44_pin3), .led1(n7408_44_pin6), .led2(n7408_44_pin8), .led3(n7408_44_pin11));
  LedBar #(.matrixcols(4)) ledbar_12 (
    .led0(n7408_45_pin3), .led1(n7408_45_pin6), .led2(n7408_45_pin8), .led3(n7408_45_pin11));
  _7408 #(.ShowInternalStructure("true"), .VccGndPorts("true")) u_7408_42 (
    .pin1(n7408_26_pin6), .pin2(n7408_38_pin1), .pin3(n7408_42_pin3), .pin4(n7408_26_pin6),
    .pin5(n7408_38_pin4), .pin6(n7408_42_pin6), .pin7(n7408_1_pin7), .pin14(n7408_1_pin14),
    .pin13(n7408_26_pin6), .pin12(n7408_38_pin13), .pin11(n7408_42_pin11), .pin10(n7408_26_pin6),
    .pin9(n7408_38_pin10), .pin8(n7408_42_pin8));
  _7408 #(.ShowInternalStructure("true"), .VccGndPorts("true")) u_7408_43 (
    .pin1(n7408_26_pin8), .pin2(n7408_39_pin1), .pin3(n7408_43_pin3), .pin4(n7408_26_pin8),
    .pin5(n7408_39_pin4), .pin6(n7408_43_pin6), .pin7(n7408_1_pin7), .pin14(n7408_1_pin14),
    .pin13(n7408_26_pin8), .pin12(n7408_39_pin13), .pin11(n7408_43_pin11), .pin10(n7408_26_pin8),
    .pin9(n7408_39_pin10), .pin8(n7408_43_pin8));
  _7408 #(.ShowInternalStructure("true"), .VccGndPorts("true")) u_7408_44 (
    .pin1(n7408_27_pin6), .pin2(n7408_40_pin1), .pin3(n7408_44_pin3), .pin4(n7408_27_pin6),
    .pin5(n7408_40_pin4), .pin6(n7408_44_pin6), .pin7(n7408_1_pin7), .pin14(n7408_1_pin14),
    .pin13(n7408_27_pin6), .pin12(n7408_40_pin13), .pin11(n7408_44_pin11), .pin10(n7408_27_pin6),
    .pin9(n7408_40_pin10), .pin8(n7408_44_pin8));
  _7408 #(.ShowInternalStructure("true"), .VccGndPorts("true")) u_7408_45 (
    .pin1(n7408_27_pin8), .pin2(n7408_41_pin1), .pin3(n7408_45_pin3), .pin4(n7408_27_pin8),
    .pin5(n7408_41_pin4), .pin6(n7408_45_pin6), .pin7(n7408_1_pin7), .pin14(n7408_1_pin14),
    .pin13(n7408_27_pin8), .pin12(n7408_41_pin13), .pin11(n7408_45_pin11), .pin10(n7408_27_pin8),
    .pin9(n7408_41_pin10), .pin8(n7408_45_pin8));
  _7408 #(.ShowInternalStructure("true"), .VccGndPorts("true")) u_7408_46 (
    .pin7(n7408_1_pin7), .pin14(n7408_1_pin14), .pin13(n7408_32_pin6), .pin12(n7408_1_pin12),
    .pin11(n7408_46_pin11));  // open: pin1, pin2, pin3, pin4, pin5, pin6, pin10, pin9, pin8
  _7404 #(.ShowInternalStructure("true"), .VccGndPorts("true")) u_7404_15 (
    .pin7(n7408_1_pin7), .pin14(n7408_1_pin14), .pin11(n7408_46_pin11), .pin10(n7404_15_pin10));  // open: pin1, pin2, pin3, pin4, pin5, pin6, pin13, pin12, pin9, pin8
  _7408 #(.ShowInternalStructure("true"), .VccGndPorts("true")) u_7408_47 (
    .pin7(n7408_1_pin7), .pin14(n7408_1_pin14), .pin13(n7408_32_pin8), .pin12(n7408_1_pin12),
    .pin11(n7408_47_pin11));  // open: pin1, pin2, pin3, pin4, pin5, pin6, pin10, pin9, pin8
  _7404 #(.ShowInternalStructure("true"), .VccGndPorts("true")) u_7404_16 (
    .pin7(n7408_1_pin7), .pin14(n7408_1_pin14), .pin11(n7408_47_pin11), .pin10(n7404_16_pin10));  // open: pin1, pin2, pin3, pin4, pin5, pin6, pin13, pin12, pin9, pin8
  _7408 #(.ShowInternalStructure("true"), .VccGndPorts("true")) u_7408_48 (
    .pin7(n7408_1_pin7), .pin14(n7408_1_pin14), .pin13(n7408_33_pin6), .pin12(n7408_1_pin12),
    .pin11(n7408_48_pin11));  // open: pin1, pin2, pin3, pin4, pin5, pin6, pin10, pin9, pin8
  _7404 #(.ShowInternalStructure("true"), .VccGndPorts("true")) u_7404_17 (
    .pin7(n7408_1_pin7), .pin14(n7408_1_pin14), .pin11(n7408_48_pin11), .pin10(n7404_17_pin10));  // open: pin1, pin2, pin3, pin4, pin5, pin6, pin13, pin12, pin9, pin8
  _7408 #(.ShowInternalStructure("true"), .VccGndPorts("true")) u_7408_49 (
    .pin7(n7408_1_pin7), .pin14(n7408_1_pin14), .pin13(n7408_33_pin8), .pin12(n7408_1_pin12),
    .pin11(n7408_49_pin11));  // open: pin1, pin2, pin3, pin4, pin5, pin6, pin10, pin9, pin8
  _7404 #(.ShowInternalStructure("true"), .VccGndPorts("true")) u_7404_18 (
    .pin7(n7408_1_pin7), .pin14(n7408_1_pin14), .pin11(n7408_49_pin11), .pin10(n7404_18_pin10));  // open: pin1, pin2, pin3, pin4, pin5, pin6, pin13, pin12, pin9, pin8
  _7432 #(.ShowInternalStructure("true"), .VccGndPorts("true")) u_7432_13 (
    .pin1(n7432_13_pin1), .pin2(n7408_2_pin8), .pin3(n7432_13_pin3), .pin4(n7432_13_pin4),
    .pin5(n7408_2_pin11), .pin6(n7432_13_pin6), .pin7(n7408_1_pin7), .pin14(n7408_1_pin14),
    .pin13(n7432_13_pin13), .pin12(n7408_2_pin3), .pin11(n7432_13_pin11), .pin10(n7432_13_pin10),
    .pin9(n7408_2_pin6), .pin8(n7432_13_pin8));
  _7432 #(.ShowInternalStructure("true"), .VccGndPorts("true")) u_7432_14 (
    .pin1(n7432_14_pin1), .pin2(n7408_2_pin8), .pin3(n7432_14_pin3), .pin4(n7432_14_pin4),
    .pin5(n7408_2_pin11), .pin6(n7432_14_pin6), .pin7(n7408_1_pin7), .pin14(n7408_1_pin14),
    .pin13(n7432_14_pin13), .pin12(n7408_2_pin3), .pin11(n7432_14_pin11), .pin10(n7432_14_pin10),
    .pin9(n7408_2_pin6), .pin8(n7432_14_pin8));
  _7408 #(.ShowInternalStructure("true"), .VccGndPorts("true")) u_7408_50 (
    .pin1(n7408_50_pin1), .pin2(n7404_16_pin10), .pin3(n7432_14_pin13), .pin4(n7408_50_pin4),
    .pin5(n7404_16_pin10), .pin6(n7432_14_pin10), .pin7(n7408_1_pin7), .pin14(n7408_1_pin14),
    .pin13(n7408_50_pin13), .pin12(n7404_16_pin10), .pin11(n7432_14_pin4), .pin10(n7408_50_pin10),
    .pin9(n7404_16_pin10), .pin8(n7432_14_pin1));
  _7432 #(.ShowInternalStructure("true"), .VccGndPorts("true")) u_7432_15 (
    .pin1(n7432_15_pin1), .pin2(n7408_2_pin8), .pin3(n7432_15_pin3), .pin4(n7432_15_pin4),
    .pin5(n7408_2_pin11), .pin6(n7432_15_pin6), .pin7(n7408_1_pin7), .pin14(n7408_1_pin14),
    .pin13(n7432_15_pin13), .pin12(n7408_2_pin3), .pin11(n7432_15_pin11), .pin10(n7432_15_pin10),
    .pin9(n7408_2_pin6), .pin8(n7432_15_pin8));
  _7408 #(.ShowInternalStructure("true"), .VccGndPorts("true")) u_7408_51 (
    .pin1(n7408_51_pin1), .pin2(n7404_17_pin10), .pin3(n7432_15_pin13), .pin4(n7408_51_pin4),
    .pin5(n7404_17_pin10), .pin6(n7432_15_pin10), .pin7(n7408_1_pin7), .pin14(n7408_1_pin14),
    .pin13(n7408_51_pin13), .pin12(n7404_17_pin10), .pin11(n7432_15_pin4), .pin10(n7408_51_pin10),
    .pin9(n7404_17_pin10), .pin8(n7432_15_pin1));
  _7432 #(.ShowInternalStructure("true"), .VccGndPorts("true")) u_7432_16 (
    .pin1(n7432_16_pin1), .pin2(n7408_2_pin8), .pin3(n7432_16_pin3), .pin4(n7432_16_pin4),
    .pin5(n7408_2_pin11), .pin6(n7432_16_pin6), .pin7(n7408_1_pin7), .pin14(n7408_1_pin14),
    .pin13(n7432_16_pin13), .pin12(n7408_2_pin3), .pin11(n7432_16_pin11), .pin10(n7432_16_pin10),
    .pin9(n7408_2_pin6), .pin8(n7432_16_pin8));
  _7408 #(.ShowInternalStructure("true"), .VccGndPorts("true")) u_7408_52 (
    .pin1(n7408_52_pin1), .pin2(n7404_18_pin10), .pin3(n7432_16_pin13), .pin4(n7408_52_pin4),
    .pin5(n7404_18_pin10), .pin6(n7432_16_pin10), .pin7(n7408_1_pin7), .pin14(n7408_1_pin14),
    .pin13(n7408_52_pin13), .pin12(n7404_18_pin10), .pin11(n7432_16_pin4), .pin10(n7408_52_pin10),
    .pin9(n7404_18_pin10), .pin8(n7432_16_pin1));
  _7408 #(.ShowInternalStructure("true"), .VccGndPorts("true")) u_7408_53 (
    .pin1(n7408_53_pin1), .pin2(n7404_15_pin10), .pin3(n7432_13_pin13), .pin4(n7408_53_pin4),
    .pin5(n7404_15_pin10), .pin6(n7432_13_pin10), .pin7(n7408_1_pin7), .pin14(n7408_1_pin14),
    .pin13(n7408_53_pin13), .pin12(n7404_15_pin10), .pin11(n7432_13_pin4), .pin10(n7408_53_pin10),
    .pin9(n7404_15_pin10), .pin8(n7432_13_pin1));
  _74175 #(.ShowInternalStructure("true"), .VccGndPorts("true")) u_74175_13 (
    .pin2(n7408_53_pin1), .pin4(n7432_13_pin11), .pin5(n7432_13_pin8), .pin7(n7408_53_pin4),
    .pin8(n7408_1_pin7), .pin16(n7408_1_pin14), .pin15(n7408_53_pin13), .pin13(n7432_13_pin6),
    .pin12(n7432_13_pin3), .pin10(n7408_53_pin10), .pin9(clock_1_out));  // open: pin1, pin3, pin6, pin14, pin11
  _74175 #(.ShowInternalStructure("true"), .VccGndPorts("true")) u_74175_14 (
    .pin2(n7408_50_pin1), .pin4(n7432_14_pin11), .pin5(n7432_14_pin8), .pin7(n7408_50_pin4),
    .pin8(n7408_1_pin7), .pin16(n7408_1_pin14), .pin15(n7408_50_pin13), .pin13(n7432_14_pin6),
    .pin12(n7432_14_pin3), .pin10(n7408_50_pin10), .pin9(clock_1_out));  // open: pin1, pin3, pin6, pin14, pin11
  _74175 #(.ShowInternalStructure("true"), .VccGndPorts("true")) u_74175_15 (
    .pin2(n7408_51_pin1), .pin4(n7432_15_pin11), .pin5(n7432_15_pin8), .pin7(n7408_51_pin4),
    .pin8(n7408_1_pin7), .pin16(n7408_1_pin14), .pin15(n7408_51_pin13), .pin13(n7432_15_pin6),
    .pin12(n7432_15_pin3), .pin10(n7408_51_pin10), .pin9(clock_1_out));  // open: pin1, pin3, pin6, pin14, pin11
  _74175 #(.ShowInternalStructure("true"), .VccGndPorts("true")) u_74175_16 (
    .pin2(n7408_52_pin1), .pin4(n7432_16_pin11), .pin5(n7432_16_pin8), .pin7(n7408_52_pin4),
    .pin8(n7408_1_pin7), .pin16(n7408_1_pin14), .pin15(n7408_52_pin13), .pin13(n7432_16_pin6),
    .pin12(n7432_16_pin3), .pin10(n7408_52_pin10), .pin9(clock_1_out));  // open: pin1, pin3, pin6, pin14, pin11
  LedBar #(.matrixcols(4)) ledbar_13 (
    .led0(n7408_54_pin3), .led1(n7408_54_pin6), .led2(n7408_54_pin8), .led3(n7408_54_pin11));
  LedBar #(.matrixcols(4)) ledbar_14 (
    .led0(n7408_55_pin3), .led1(n7408_55_pin6), .led2(n7408_55_pin8), .led3(n7408_55_pin11));
  LedBar #(.matrixcols(4)) ledbar_15 (
    .led0(n7408_56_pin3), .led1(n7408_56_pin6), .led2(n7408_56_pin8), .led3(n7408_56_pin11));
  LedBar #(.matrixcols(4)) ledbar_16 (
    .led0(n7408_57_pin3), .led1(n7408_57_pin6), .led2(n7408_57_pin8), .led3(n7408_57_pin11));
  _7408 #(.ShowInternalStructure("true"), .VccGndPorts("true")) u_7408_54 (
    .pin1(n7408_32_pin6), .pin2(n7408_53_pin1), .pin3(n7408_54_pin3), .pin4(n7408_32_pin6),
    .pin5(n7408_53_pin4), .pin6(n7408_54_pin6), .pin7(n7408_1_pin7), .pin14(n7408_1_pin14),
    .pin13(n7408_32_pin6), .pin12(n7408_53_pin13), .pin11(n7408_54_pin11), .pin10(n7408_32_pin6),
    .pin9(n7408_53_pin10), .pin8(n7408_54_pin8));
  _7408 #(.ShowInternalStructure("true"), .VccGndPorts("true")) u_7408_55 (
    .pin1(n7408_32_pin8), .pin2(n7408_50_pin1), .pin3(n7408_55_pin3), .pin4(n7408_32_pin8),
    .pin5(n7408_50_pin4), .pin6(n7408_55_pin6), .pin7(n7408_1_pin7), .pin14(n7408_1_pin14),
    .pin13(n7408_32_pin8), .pin12(n7408_50_pin13), .pin11(n7408_55_pin11), .pin10(n7408_32_pin8),
    .pin9(n7408_50_pin10), .pin8(n7408_55_pin8));
  _7408 #(.ShowInternalStructure("true"), .VccGndPorts("true")) u_7408_56 (
    .pin1(n7408_33_pin6), .pin2(n7408_51_pin1), .pin3(n7408_56_pin3), .pin4(n7408_33_pin6),
    .pin5(n7408_51_pin4), .pin6(n7408_56_pin6), .pin7(n7408_1_pin7), .pin14(n7408_1_pin14),
    .pin13(n7408_33_pin6), .pin12(n7408_51_pin13), .pin11(n7408_56_pin11), .pin10(n7408_33_pin6),
    .pin9(n7408_51_pin10), .pin8(n7408_56_pin8));
  _7408 #(.ShowInternalStructure("true"), .VccGndPorts("true")) u_7408_57 (
    .pin1(n7408_33_pin8), .pin2(n7408_52_pin1), .pin3(n7408_57_pin3), .pin4(n7408_33_pin8),
    .pin5(n7408_52_pin4), .pin6(n7408_57_pin6), .pin7(n7408_1_pin7), .pin14(n7408_1_pin14),
    .pin13(n7408_33_pin8), .pin12(n7408_52_pin13), .pin11(n7408_57_pin11), .pin10(n7408_33_pin8),
    .pin9(n7408_52_pin10), .pin8(n7408_57_pin8));
  // also tied to GND on the sheet: n7408_1_pin7
  // also tied to VCC on the sheet: {n7408_14_pin5, n7408_1_pin14}
endmodule
