// Logisim project 4_digit_MEMORY_READ_WRITE.circ as structural Verilog: 1 circuit, main circuit main
module main (
);

  wire clock_1_out, dipswitch_1_p1, dipswitch_1_p2, dipswitch_1_p3, dipswitch_1_p4, dipswitch_3_p1,
       dipswitch_3_p2, n7404_1_pin2, n7404_1_pin4, n7404_1_pin8, n7404_1_pin12, n7408_1_pin1, n7408_1_pin3,
       n7408_1_pin6, n7408_1_pin7, n7408_1_pin8, n7408_1_pin11, n7408_1_pin14, n7408_2_pin1, n7408_2_pin2,
       n7408_2_pin3, n7408_2_pin4, n7408_2_pin6, n7408_2_pin8, n7408_2_pin10, n7408_2_pin11, n7408_2_pin13,
       n7408_3_pin1, n7408_3_pin3, n7408_3_pin4, n7408_3_pin6, n7408_3_pin8, n7408_3_pin10, n7408_3_pin11,
       n7408_3_pin13, n7408_4_pin1, n7408_4_pin3, n7408_4_pin4, n7408_4_pin6, n7408_4_pin8, n7408_4_pin10,
       n7408_4_pin11, n7408_4_pin13, n7408_5_pin1, n7408_5_pin3, n7408_5_pin4, n7408_5_pin6, n7408_5_pin8,
       n7408_5_pin10, n7408_5_pin11, n7408_5_pin13, n7432_1_pin3, n7432_1_pin6, n7432_1_pin8, n7432_1_pin11,
       n7432_2_pin3, n7432_2_pin6, n7432_2_pin8, n7432_2_pin11, n7432_3_pin3, n7432_3_pin6, n7432_3_pin8,
       n7432_3_pin11, n7432_4_pin3, n7432_4_pin6, n7432_4_pin8, n7432_4_pin11, n74139_1_pin4, n74139_1_pin5,
       n74139_1_pin6, n74139_1_pin7;

  Clock clock_1 (.out(clock_1_out));
  LedBar #(.matrixcols(4)) ledbar_1 (
    .led0(n7408_1_pin3), .led1(n7408_1_pin6), .led2(n7408_1_pin11), .led3(n7408_1_pin8));
  // DipSwitch #(.number(4)) dipswitch_1: pin names not known; wires that end beside it: dipswitch_1_p1, dipswitch_1_p2, dipswitch_1_p3, dipswitch_1_p4
  _7408 #(.ShowInternalStructure("true"), .VccGndPorts("true")) u_7408_1 (
    .pin1(n7408_1_pin1), .pin2(dipswitch_1_p1), .pin3(n7408_1_pin3), .pin4(n7408_1_pin1),
    .pin5(dipswitch_1_p2), .pin6(n7408_1_pin6), .pin7(n7408_1_pin7), .pin14(n7408_1_pin14),
    .pin13(n7408_1_pin1), .pin12(dipswitch_1_p3), .pin11(n7408_1_pin11), .pin10(n7408_1_pin1),
    .pin9(dipswitch_1_p4), .pin8(n7408_1_pin8));
  LED led_1 (.in(n7408_1_pin1));
  LED led_2 (.in(n7408_1_pin1));
  LED led_3 (.in(n7408_1_pin1));
  LED led_4 (.in(n7408_1_pin1));
  LED led_5 (.in(n7408_1_pin1));
  // DipSwitch #(.number(1)) dipswitch_2: pin names not known
  _7408 #(.ShowInternalStructure("true"), .VccGndPorts("true")) u_7408_2 (
    .pin1(n7408_2_pin1), .pin2(n7408_2_pin2), .pin3(n7408_2_pin3), .pin4(n7408_2_pin4), .pin5(n7408_2_pin2),
    .pin6(n7408_2_pin6), .pin7(n7408_1_pin7), .pin14(n7408_1_pin14), .pin13(n7408_2_pin13),
    .pin12(n7408_2_pin2), .pin11(n7408_2_pin11), .pin10(n7408_2_pin10), .pin9(n7408_2_pin2),
    .pin8(n7408_2_pin8));
  // DipSwitch #(.number(2)) dipswitch_3: pin names not known; wires that end beside it: dipswitch_3_p1, dipswitch_3_p2
  _74139 #(.ShowInternalStructure("true"), .VccGndPorts("true")) u_74139_1 (
    .pin1(n7408_1_pin7), .pin2(dipswitch_3_p2), .pin3(dipswitch_3_p1), .pin4(n74139_1_pin4),
    .pin5(n74139_1_pin5), .pin6(n74139_1_pin6), .pin7(n74139_1_pin7), .pin8(n7408_1_pin7),
    .pin16(n7408_1_pin14));  // open: pin15, pin14, pin13, pin12, pin11, pin10, pin9
  _7432 #(.ShowInternalStructure("true"), .VccGndPorts("true")) u_7432_1 (
    .pin1(n7408_2_pin11), .pin2(n7408_1_pin3), .pin3(n7432_1_pin3), .pin4(n7408_2_pin8), .pin5(n7408_1_pin6),
    .pin6(n7432_1_pin6), .pin7(n7408_1_pin7), .pin14(n7408_1_pin14), .pin13(n7408_2_pin6),
    .pin12(n7408_1_pin11), .pin11(n7432_1_pin11), .pin10(n7408_2_pin3), .pin9(n7408_1_pin8),
    .pin8(n7432_1_pin8));
  _74175 #(.ShowInternalStructure("true"), .VccGndPorts("true")) u_74175_1 (
    .pin2(n7408_2_pin13), .pin4(n7432_1_pin3), .pin5(n7432_1_pin6), .pin7(n7408_2_pin10),
    .pin8(n7408_1_pin7), .pin16(n7408_1_pin14), .pin15(n7408_2_pin1), .pin13(n7432_1_pin8),
    .pin12(n7432_1_pin11), .pin10(n7408_2_pin4), .pin9(clock_1_out));  // open: pin1, pin3, pin6, pin14, pin11
  _7404 #(.ShowInternalStructure("true"), .VccGndPorts("true")) u_7404_1 (
    .pin1(n74139_1_pin6), .pin2(n7404_1_pin2), .pin3(n74139_1_pin7), .pin4(n7404_1_pin4),
    .pin7(n7408_1_pin7), .pin14(n7408_1_pin14), .pin13(n74139_1_pin5), .pin12(n7404_1_pin12),
    .pin11(n74139_1_pin4), .pin10(n7408_2_pin2), .pin9(n7408_1_pin1), .pin8(n7404_1_pin8));  // open: pin5, pin6
  LedBar #(.matrixcols(4)) ledbar_2 (
    .led0(n7408_2_pin13), .led1(n7408_2_pin10), .led2(n7408_2_pin4), .led3(n7408_2_pin1));
  _7408 #(.ShowInternalStructure("true"), .VccGndPorts("true")) u_7408_3 (
    .pin1(n7408_3_pin1), .pin2(n7404_1_pin12), .pin3(n7408_3_pin3), .pin4(n7408_3_pin4),
    .pin5(n7404_1_pin12), .pin6(n7408_3_pin6), .pin7(n7408_1_pin7), .pin14(n7408_1_pin14),
    .pin13(n7408_3_pin13), .pin12(n7404_1_pin12), .pin11(n7408_3_pin11), .pin10(n7408_3_pin10),
    .pin9(n7404_1_pin12), .pin8(n7408_3_pin8));
  _7432 #(.ShowInternalStructure("true"), .VccGndPorts("true")) u_7432_2 (
    .pin1(n7408_3_pin11), .pin2(n7408_1_pin3), .pin3(n7432_2_pin3), .pin4(n7408_3_pin8), .pin5(n7408_1_pin6),
    .pin6(n7432_2_pin6), .pin7(n7408_1_pin7), .pin14(n7408_1_pin14), .pin13(n7408_3_pin6),
    .pin12(n7408_1_pin11), .pin11(n7432_2_pin11), .pin10(n7408_3_pin3), .pin9(n7408_1_pin8),
    .pin8(n7432_2_pin8));
  _74175 #(.ShowInternalStructure("true"), .VccGndPorts("true")) u_74175_2 (
    .pin2(n7408_3_pin13), .pin4(n7432_2_pin3), .pin5(n7432_2_pin6), .pin7(n7408_3_pin10),
    .pin8(n7408_1_pin7), .pin16(n7408_1_pin14), .pin15(n7408_3_pin1), .pin13(n7432_2_pin8),
    .pin12(n7432_2_pin11), .pin10(n7408_3_pin4), .pin9(clock_1_out));  // open: pin1, pin3, pin6, pin14, pin11
  LedBar #(.matrixcols(4)) ledbar_3 (
    .led0(n7408_3_pin13), .led1(n7408_3_pin10), .led2(n7408_3_pin4), .led3(n7408_3_pin1));
  _7408 #(.ShowInternalStructure("true"), .VccGndPorts("true")) u_7408_4 (
    .pin1(n7408_4_pin1), .pin2(n7404_1_pin4), .pin3(n7408_4_pin3), .pin4(n7408_4_pin4), .pin5(n7404_1_pin4),
    .pin6(n7408_4_pin6), .pin7(n7408_1_pin7), .pin14(n7408_1_pin14), .pin13(n7408_4_pin13),
    .pin12(n7404_1_pin4), .pin11(n7408_4_pin11), .pin10(n7408_4_pin10), .pin9(n7404_1_pin4),
    .pin8(n7408_4_pin8));
  _7408 #(.ShowInternalStructure("true"), .VccGndPorts("true")) u_7408_5 (
    .pin1(n7408_5_pin1), .pin2(n7404_1_pin2), .pin3(n7408_5_pin3), .pin4(n7408_5_pin4), .pin5(n7404_1_pin2),
    .pin6(n7408_5_pin6), .pin7(n7408_1_pin7), .pin14(n7408_1_pin14), .pin13(n7408_5_pin13),
    .pin12(n7404_1_pin2), .pin11(n7408_5_pin11), .pin10(n7408_5_pin10), .pin9(n7404_1_pin2),
    .pin8(n7408_5_pin8));
  _7432 #(.ShowInternalStructure("true"), .VccGndPorts("true")) u_7432_3 (
    .pin1(n7408_4_pin11), .pin2(n7408_1_pin3), .pin3(n7432_3_pin3), .pin4(n7408_4_pin8), .pin5(n7408_1_pin6),
    .pin6(n7432_3_pin6), .pin7(n7408_1_pin7), .pin14(n7408_1_pin14), .pin13(n7408_4_pin6),
    .pin12(n7408_1_pin11), .pin11(n7432_3_pin11), .pin10(n7408_4_pin3), .pin9(n7408_1_pin8),
    .pin8(n7432_3_pin8));
  _7432 #(.ShowInternalStructure("true"), .VccGndPorts("true")) u_7432_4 (
    .pin1(n7408_5_pin11), .pin2(n7408_1_pin3), .pin3(n7432_4_pin3), .pin4(n7408_5_pin8), .pin5(n7408_1_pin6),
    .pin6(n7432_4_pin6), .pin7(n7408_1_pin7), .pin14(n7408_1_pin14), .pin13(n7408_5_pin6),
    .pin12(n7408_1_pin11), .pin11(n7432_4_pin11), .pin10(n7408_5_pin3), .pin9(n7408_1_pin8),
    .pin8(n7432_4_pin8));
  _74175 #(.ShowInternalStructure("true"), .VccGndPorts("true")) u_74175_3 (
    .pin2(n7408_4_pin13), .pin4(n7432_3_pin3), .pin5(n7432_3_pin6), .pin7(n7408_4_pin10),
    .pin8(n7408_1_pin7), .pin16(n7408_1_pin14), .pin15(n7408_4_pin1), .pin13(n7432_3_pin8),
    .pin12(n7432_3_pin11), .pin10(n7408_4_pin4), .pin9(clock_1_out));  // open: pin1, pin3, pin6, pin14, pin11
  _74175 #(.ShowInternalStructure("true"), .VccGndPorts("true")) u_74175_4 (
    .pin2(n7408_5_pin13), .pin4(n7432_4_pin3), .pin5(n7432_4_pin6), .pin7(n7408_5_pin10),
    .pin8(n7408_1_pin7), .pin16(n7408_1_pin14), .pin15(n7408_5_pin1), .pin13(n7432_4_pin8),
    .pin12(n7432_4_pin11), .pin10(n7408_5_pin4), .pin9(clock_1_out));  // open: pin1, pin3, pin6, pin14, pin11
  LedBar #(.matrixcols(4)) ledbar_4 (
    .led0(n7408_4_pin13), .led1(n7408_4_pin10), .led2(n7408_4_pin4), .led3(n7408_4_pin1));
  LedBar #(.matrixcols(4)) ledbar_5 (
    .led0(n7408_5_pin13), .led1(n7408_5_pin10), .led2(n7408_5_pin4), .led3(n7408_5_pin1));
  // also tied to GND on the sheet: n7408_1_pin7
  // also tied to VCC on the sheet: n7408_1_pin14
endmodule
